# Fritzing sketch arduino-bluetooth (saved by Fritzing 0.9.1b)
circuit board: 8.46667cm x 5.64444cm

parts:
  Parte1 = Bluetooth Module Breakout - Roving Networks (RN-41)
  Parte3 = Arduino Uno (Rev3)
  M1 = DC Motor

nets:
  VCC: Parte1.VCC, Parte3.3V3
  GND: Parte1.GND, Parte3.GND, M1.pin_1
  N1: Parte1.UARTTX, Parte3.D11_PWM/MOSI
  N2: Parte1.UARTRX, Parte3.D10_PWM/SS
  N3: Parte3.D12/MISO, M1.pin_2
